// Logisim project DigitalLogic2.circ as structural Verilog: 12 circuits, main circuit 4x2Encoder
module SignExtend (
  input  [7:0] in_1,
  output [15:0] out_2
);


  assign out_2 = {{9{in_1[7]}}, in_1[6:0]};

  // Notes on the sheet:
  //   Sign Extend
endmodule

module _4x2Encoder (
  input  [3:0] Input,
  output [1:0] Output
);

  wire and_1_out, and_2_out, and_3_out, not_1_out, not_2_out, not_3_out, not_4_out;

  not not_1 (not_1_out, Input[3]);
  not not_2 (not_2_out, Input[2]);
  not not_3 (not_3_out, Input[0]);
  not not_4 (not_4_out, Input[1]);
  and and_1 (and_1_out, not_1_out, Input[2], not_4_out, not_3_out);
  and and_2 (and_2_out, Input[3], not_2_out, not_4_out, not_3_out);
  and and_3 (and_3_out, not_1_out, not_2_out, Input[1], not_3_out);
  or or_1 (Output[1], and_1_out, and_2_out);
  or or_2 (Output[0], and_2_out, and_3_out);

  // Notes on the sheet:
  //   4x2 Encoder
endmodule

module _8x3Encoder (
  input  [7:0] Inputs,
  output [2:0] Ouput
);

  wire I_1_out, I_2_out, I_3_out, I_4_out, I_5_out, I_6_out, I_7_out, not_1_out, not_2_out, not_3_out,
       not_4_out, not_5_out, not_6_out, not_7_out, not_8_out;

  not not_1 (not_1_out, Inputs[7]);
  not not_2 (not_2_out, Inputs[5]);
  not not_3 (not_3_out, Inputs[6]);
  not not_4 (not_4_out, Inputs[4]);
  not not_5 (not_5_out, Inputs[3]);
  not not_6 (not_6_out, Inputs[1]);
  not not_7 (not_7_out, Inputs[2]);
  not not_8 (not_8_out, Inputs[0]);
  and I_4 (I_4_out, not_1_out, not_3_out, not_2_out, Inputs[4], not_5_out, not_7_out, not_6_out, not_8_out);
  and I_5 (I_5_out, not_1_out, not_3_out, Inputs[5], not_4_out, not_5_out, not_7_out, not_6_out, not_8_out);
  and I_6 (I_6_out, not_1_out, Inputs[6], not_2_out, not_4_out, not_5_out, not_7_out, not_6_out, not_8_out);
  and I_3 (I_3_out, not_1_out, not_3_out, not_2_out, not_4_out, Inputs[3], not_7_out, not_6_out, not_8_out);
  and I_7 (I_7_out, Inputs[7], not_3_out, not_2_out, not_4_out, not_5_out, not_7_out, not_6_out, not_8_out);
  and I_2 (I_2_out, not_1_out, not_3_out, not_2_out, not_4_out, not_5_out, Inputs[2], not_6_out, not_8_out);
  and I_1 (I_1_out, not_1_out, not_3_out, not_2_out, not_4_out, not_5_out, not_7_out, Inputs[1], not_8_out);
  or or_1 (Ouput[2], I_4_out, I_5_out, I_6_out, I_7_out);
  or or_2 (Ouput[1], I_6_out, I_7_out, I_3_out, I_2_out);
  or or_3 (Ouput[0], I_7_out, I_5_out, I_3_out, I_1_out);

  // Notes on the sheet:
  //   8x3 Encoder
endmodule

module _2x4Decoder (
  input  [1:0] Input,
  output [3:0] Output
);

  wire not_1_out, not_2_out;

  not not_1 (not_1_out, Input[1]);
  not not_2 (not_2_out, Input[0]);
  and and_1 (Output[0], not_2_out, not_1_out);
  and and_2 (Output[1], Input[0], not_1_out);
  and and_3 (Output[2], not_2_out, Input[1]);
  and and_4 (Output[3], Input[0], Input[1]);

  // Notes on the sheet:
  //   2x4 Decoder
endmodule

module _3x8Decoder (
  input  [2:0] Inputs,
  output [7:0] Output
);

  wire not_1_out, not_2_out, not_3_out;

  not not_1 (not_1_out, Inputs[2]);
  not not_2 (not_2_out, Inputs[1]);
  not not_3 (not_3_out, Inputs[0]);
  and and_1 (Output[0], not_3_out, not_2_out, not_1_out);
  and and_2 (Output[1], Inputs[0], not_2_out, not_1_out);
  and and_3 (Output[2], not_3_out, Inputs[1], not_1_out);
  and and_4 (Output[3], Inputs[0], Inputs[1], not_1_out);
  and and_5 (Output[4], not_3_out, not_2_out, Inputs[2]);
  and and_6 (Output[5], Inputs[0], not_2_out, Inputs[2]);
  and and_7 (Output[6], not_3_out, Inputs[1], Inputs[2]);
  and and_8 (Output[7], Inputs[0], Inputs[1], Inputs[2]);

  // Notes on the sheet:
  //   3x8 Decoder
endmodule

module _4x1Multiplexer (
  input  I_0,
  input  I_1,
  input  I_2,
  input  I_3,
  input  [1:0] Select,
  output out_6
);

  wire and_1_out, and_2_out, and_3_out, and_4_out, decoder_1_out0, decoder_1_out1, decoder_1_out2,
       decoder_1_out3;

  Decoder #(.select(2)) decoder_1 (
    .out0(decoder_1_out0), .out1(decoder_1_out1), .out2(decoder_1_out2), .out3(decoder_1_out3), .sel(Select));  // open: en
  and and_1 (and_1_out, I_0, decoder_1_out0);
  and and_2 (and_2_out, I_1, decoder_1_out1);
  and and_3 (and_3_out, I_2, decoder_1_out2);
  and and_4 (and_4_out, I_3, decoder_1_out3);
  or or_1 (out_6, and_1_out, and_2_out, and_3_out, and_4_out);

  // Notes on the sheet:
  //   4x1 Multiplexer
endmodule

module _8x1Multiplexer (
  input  I_0,
  input  I_1,
  input  I_2,
  input  I_3,
  input  I_4,
  input  I_5,
  input  I_6,
  input  I_7,
  input  [2:0] Select,
  output out_10
);

  wire and_1_out, and_2_out, and_3_out, and_4_out, and_5_out, and_6_out, and_7_out, and_8_out,
       decoder_1_out0, decoder_1_out1, decoder_1_out2, decoder_1_out3, decoder_1_out4, decoder_1_out5,
       decoder_1_out6, decoder_1_out7;

  Decoder #(.select(3)) decoder_1 (
    .out0(decoder_1_out0), .out1(decoder_1_out1), .out2(decoder_1_out2), .out3(decoder_1_out3),
    .out4(decoder_1_out4), .out5(decoder_1_out5), .out6(decoder_1_out6), .out7(decoder_1_out7), .sel(Select));  // open: en
  and and_1 (and_1_out, I_0, decoder_1_out0);
  and and_2 (and_2_out, I_1, decoder_1_out1);
  and and_3 (and_3_out, I_2, decoder_1_out2);
  and and_4 (and_4_out, I_3, decoder_1_out3);
  and and_5 (and_5_out, I_4, decoder_1_out4);
  and and_6 (and_6_out, I_5, decoder_1_out5);
  and and_7 (and_7_out, I_6, decoder_1_out6);
  and and_8 (and_8_out, I_7, decoder_1_out7);
  or or_1 (out_10, and_1_out, and_2_out, and_3_out, and_4_out, and_5_out, and_6_out, and_7_out, and_8_out);

  // Notes on the sheet:
  //   8x1 Multiplexer
endmodule

module AbstractedMultiplexers (
  input  I_0,
  input  [3:0] I_0_2,
  input  I_1,
  input  [3:0] I_1_2,
  input  I_2,
  input  [3:0] I_2_2,
  input  [15:0] I_0_3,
  input  I_3,
  input  [3:0] I_3_2,
  input  [1:0] Select,
  input  [1:0] Select_2,
  input  [15:0] I_1_3,
  input  [15:0] I_2_3,
  input  [15:0] I_3_3,
  input  I_0_4,
  input  [3:0] I_0_5,
  input  [15:0] I_4,
  input  I_1_4,
  input  [3:0] I_1_5,
  input  I_2_4,
  input  [3:0] I_2_5,
  input  [15:0] I_5,
  input  I_3_4,
  input  [3:0] I_3_5,
  input  [15:0] I_6,
  input  I_4_2,
  input  [3:0] I_4_3,
  input  I_5_2,
  input  [3:0] I_5_3,
  input  [15:0] I_7,
  input  I_6_2,
  input  [3:0] I_6_3,
  input  I_7_2,
  input  [3:0] I_7_3,
  input  [2:0] Select_3,
  input  [2:0] Select_4,
  input  [2:0] Select_5,
  output out_38,
  output [3:0] out_39,
  output [15:0] out_40,
  output out_41,
  output [3:0] out_42
);

  Multiplexer #(.select(2), .enable("false")) multiplexer_1 (
    .in0(I_0), .in1(I_1), .in2(I_2), .in3(I_3), .out(out_38), .sel(Select));
  Multiplexer #(.select(3), .enable("false")) multiplexer_2 (
    .in0(I_0_4), .in1(I_1_4), .in2(I_2_4), .in3(I_3_4), .in4(I_4_2), .in5(I_5_2), .in6(I_6_2), .in7(I_7_2),
    .out(out_41), .sel(Select_4));
  Multiplexer #(.select(2), .width(4), .enable("false")) multiplexer_3 (
    .in0(I_0_2), .in1(I_1_2), .in2(I_2_2), .in3(I_3_2), .out(out_39), .sel(Select_2));
  Multiplexer #(.select(3), .width(4), .enable("false")) multiplexer_4 (
    .in0(I_0_5), .in1(I_1_5), .in2(I_2_5), .in3(I_3_5), .in4(I_4_3), .in5(I_5_3), .in6(I_6_3), .in7(I_7_3),
    .out(out_42), .sel(Select_5));
  Multiplexer #(.select(3), .width(16), .enable("false")) multiplexer_5 (
    .in0(I_0_3), .in1(I_1_3), .in2(I_2_3), .in3(I_3_3), .in4(I_4), .in5(I_5), .in6(I_6), .in7(I_7),
    .out(out_40), .sel(Select_3));

  // Notes on the sheet:
  //   Abstracted 4x1 MUX
  //   Abstracted 8x1 MUX
  //   Abstracted 4x4 MUX
  //   Abstracted 8x4 MUX
  //   Abstracted 8x16
endmodule

module _1x4Demultiplexer (
  input  I,
  input  [1:0] Select,
  output D_0,
  output D_1,
  output D_2,
  output D_3
);

  wire decoder_1_out0, decoder_1_out1, decoder_1_out2, decoder_1_out3;

  Decoder #(.select(2)) decoder_1 (
    .out0(decoder_1_out0), .out1(decoder_1_out1), .out2(decoder_1_out2), .out3(decoder_1_out3), .sel(Select));  // open: en
  and and_1 (D_0, I, decoder_1_out0);
  and and_2 (D_1, I, decoder_1_out1);
  and and_3 (D_2, I, decoder_1_out2);
  and and_4 (D_3, I, decoder_1_out3);

  // Notes on the sheet:
  //   1x4 Demultiplexer
endmodule

module _1x8Demultiplexer (
  input  I,
  input  [2:0] Select,
  output D_0,
  output D_1,
  output D_2,
  output D_3,
  output D_4,
  output D_5,
  output D_6,
  output D_7
);

  wire decoder_1_out0, decoder_1_out1, decoder_1_out2, decoder_1_out3, decoder_1_out4, decoder_1_out5,
       decoder_1_out6, decoder_1_out7;

  Decoder #(.select(3)) decoder_1 (
    .out0(decoder_1_out0), .out1(decoder_1_out1), .out2(decoder_1_out2), .out3(decoder_1_out3),
    .out4(decoder_1_out4), .out5(decoder_1_out5), .out6(decoder_1_out6), .out7(decoder_1_out7), .sel(Select));  // open: en
  and and_1 (D_0, I, decoder_1_out0);
  and and_2 (D_1, I, decoder_1_out1);
  and and_3 (D_2, I, decoder_1_out2);
  and and_4 (D_3, I, decoder_1_out3);
  and and_5 (D_4, I, decoder_1_out4);
  and and_6 (D_5, I, decoder_1_out5);
  and and_7 (D_6, I, decoder_1_out6);
  and and_8 (D_7, I, decoder_1_out7);

  // Notes on the sheet:
  //   1x8 Demultiplexer
endmodule

module AbstractedDemultiplexers (
  input  in_1,
  input  [3:0] in_2,
  input  [1:0] Select,
  input  [1:0] Select_2,
  input  [15:0] I,
  input  [2:0] Select_3,
  input  in_7,
  input  [3:0] in_8,
  input  [2:0] Select_4,
  input  [2:0] Select_5,
  output D_0,
  output [3:0] D_0_2,
  output D_1,
  output [3:0] D_1_2,
  output [15:0] D_0_3,
  output D_2,
  output [3:0] D_2_2,
  output [15:0] D_1_3,
  output D_3,
  output [3:0] D_3_2,
  output [15:0] D_2_3,
  output [15:0] D_3_3,
  output D_0_4,
  output [3:0] D_0_5,
  output [15:0] D_4,
  output D_1_4,
  output [3:0] D_1_5,
  output D_2_4,
  output [15:0] D_5,
  output [3:0] D_2_5,
  output D_3_4,
  output [3:0] D_3_5,
  output [15:0] D_6,
  output D_4_2,
  output [3:0] D_4_3,
  output D_5_2,
  output [3:0] D_5_3,
  output [15:0] D_7,
  output D_6_2,
  output [3:0] D_6_3,
  output D_7_2,
  output [3:0] D_7_3
);

  Demultiplexer #(.select(2), .enable("false")) demultiplexer_1 (
    .out0(D_0), .out1(D_1), .out2(D_2), .out3(D_3), .in(in_1), .sel(Select));
  Demultiplexer #(.select(3), .enable("false")) demultiplexer_2 (
    .out0(D_0_4), .out1(D_1_4), .out2(D_2_4), .out3(D_3_4), .out4(D_4_2), .out5(D_5_2), .out6(D_6_2),
    .out7(D_7_2), .in(in_7), .sel(Select_4));
  Demultiplexer #(.select(2), .width(4), .enable("false")) demultiplexer_3 (
    .out0(D_0_2), .out1(D_1_2), .out2(D_2_2), .out3(D_3_2), .in(in_2), .sel(Select_2));
  Demultiplexer #(.select(3), .width(4), .enable("false")) demultiplexer_4 (
    .out0(D_0_5), .out1(D_1_5), .out2(D_2_5), .out3(D_3_5), .out4(D_4_3), .out5(D_5_3), .out6(D_6_3),
    .out7(D_7_3), .in(in_8), .sel(Select_5));
  Demultiplexer #(.select(3), .width(16), .enable("false")) demultiplexer_5 (
    .out0(D_0_3), .out1(D_1_3), .out2(D_2_3), .out3(D_3_3), .out4(D_4), .out5(D_5), .out6(D_6), .out7(D_7),
    .in(I), .sel(Select_3));

  // Notes on the sheet:
  //   Abstracted 1x4 DMX
  //   Abstracted 1x8 DMX
  //   Abstracted 4x4 DMX
  //   Abstracted 4x8 DMX
  //   Abstracted 8x16 DMX with Buses
endmodule

module MUXtoDMX (
  input  [15:0] I_0,
  input  [15:0] I_1,
  input  [15:0] I_2,
  input  [15:0] I_3,
  input  [15:0] I_4,
  input  [15:0] I_5,
  input  [2:0] Select,
  input  [2:0] Select_2,
  input  [15:0] I_6,
  input  [15:0] I_7,
  output [15:0] D_0,
  output [15:0] D_1,
  output [15:0] D_2,
  output [15:0] D_3,
  output [15:0] D_4,
  output [15:0] D_5,
  output [15:0] D_6,
  output [15:0] D_7
);

  wire [15:0] multiplexer_1_out;

  Multiplexer #(.select(3), .width(16)) multiplexer_1 (
    .in0(I_0), .in1(I_1), .in2(I_2), .in3(I_3), .in4(I_4), .in5(I_5), .in6(I_6), .in7(I_7),
    .out(multiplexer_1_out), .sel(Select));  // open: en
  Demultiplexer #(.select(3), .width(16)) demultiplexer_1 (
    .out0(D_0), .out1(D_1), .out2(D_2), .out3(D_3), .out4(D_4), .out5(D_5), .out6(D_6), .out7(D_7),
    .in(multiplexer_1_out), .sel(Select_2));  // open: en

  // Notes on the sheet:
  //   INPUT BUSES
  //   OUTPUT BUSES
endmodule
