// Logisim project DigitalLogic3.circ as structural Verilog: 6 circuits, main circuit HalfAdder
module HalfAdder (
  input  X_0,
  input  X_1,
  output C__Carry_Out,
  output S__Sum
);

  and and_1 (C__Carry_Out, X_0, X_1);
  xor xor_1 (S__Sum, X_0, X_1);
endmodule

module FullAdder (
  input  X_0,
  input  X_1,
  input  C_in,
  output C_out,
  output S
);

  wire and_1_out, and_2_out, xor_1_out;

  and and_1 (and_1_out, X_0, X_1);
  xor xor_1 (xor_1_out, X_0, X_1);
  and and_2 (and_2_out, xor_1_out, C_in);
  or or_1 (C_out, and_1_out, and_2_out);
  xor xor_2 (S, xor_1_out, C_in);
endmodule

module AbstractedAdder (
  input  C_in,
  input  X_0,
  input  X_1,
  output S,
  output C_out
);

  Adder #(.width(1)) adder_1 (.a(X_0), .b(X_1), .out(S), .cin(C_in), .cout(C_out));
endmodule

module _2bitAdder (
  input  X_1,
  input  X_0,
  input  Y_1,
  input  Y_0,
  output S_0,
  output S_1,
  output Carry_Out
);

  wire adder_1_cout;

  Adder #(.width(1)) adder_1 (.a(Y_0), .b(X_0), .out(S_0), .cin(1'b0), .cout(adder_1_cout));
  Adder #(.width(1)) adder_2 (.a(Y_1), .b(X_1), .out(S_1), .cin(adder_1_cout), .cout(Carry_Out));
endmodule

module _3bitAdder (
  input  X_2,
  input  X_1,
  input  X_0,
  input  Y_2,
  input  Y_1,
  input  Y_0,
  output S_0,
  output S_1,
  output S_2,
  output Carry_Out
);

  wire adder_1_cout, adder_2_cout;

  Adder #(.width(1)) adder_1 (.a(Y_0), .b(X_0), .out(S_0), .cin(1'b0), .cout(adder_1_cout));
  Adder #(.width(1)) adder_2 (.a(Y_1), .b(X_1), .out(S_1), .cin(adder_1_cout), .cout(adder_2_cout));
  Adder #(.width(1)) adder_3 (.a(Y_2), .b(X_2), .out(S_2), .cin(adder_2_cout), .cout(Carry_Out));
endmodule

module _4bitAdder (
  input  [3:0] X,
  input  [3:0] Y,
  output [4:0] Output
);

  wire adder_1_cout, adder_2_cout, adder_3_cout;

  Adder #(.width(1)) adder_1 (.a(Y[0]), .b(X[0]), .out(Output[0]), .cin(1'b0), .cout(adder_1_cout));
  Adder #(.width(1)) adder_2 (.a(Y[1]), .b(X[1]), .out(Output[1]), .cin(adder_1_cout), .cout(adder_2_cout));
  Adder #(.width(1)) adder_3 (.a(Y[2]), .b(X[2]), .out(Output[2]), .cin(adder_2_cout), .cout(adder_3_cout));
  Adder #(.width(1)) adder_4 (.a(Y[3]), .b(X[3]), .out(Output[3]), .cin(adder_3_cout), .cout(Output[4]));
endmodule
