// Logisim project MemoryArch1.circ as structural Verilog: 12 circuits, main circuit SRLatch
module SRLatch (
  input  S,
  input  R,
  output nQ,
  output Q
);

  nor nor_1 (nQ, S, Q);
  nor nor_2 (Q, nQ, R);
endmodule

module SRFlipFlop (
  input  S,
  input  R,
  output nQ,
  output Q
);

  wire and_1_out, and_2_out, clock_1_out;

  Clock clock_1 (.out(clock_1_out));
  and and_1 (and_1_out, S, clock_1_out);
  and and_2 (and_2_out, clock_1_out, R);
  nor nor_1 (nQ, and_1_out, Q);
  nor nor_2 (Q, nQ, and_2_out);
endmodule

module DFlipFlop (
  input  D,
  output nQ,
  output Q
);

  wire and_1_out, and_2_out, clock_1_out, not_1_out;

  Clock clock_1 (.out(clock_1_out));
  not not_1 (not_1_out, D);
  and and_1 (and_1_out, D, clock_1_out);
  and and_2 (and_2_out, clock_1_out, not_1_out);
  nor nor_1 (nQ, and_1_out, Q);
  nor nor_2 (Q, nQ, and_2_out);
endmodule

module JKFlipFlop (
  input  J,
  input  K,
  output Q,
  output nQ
);

  wire clock_1_out;

  Clock clock_1 (.out(clock_1_out));
  J_K_Flip_Flop j_k_ff_1 (.J(J), .clk(clock_1_out), .K(K), .Q(Q), .Qn(nQ));  // open: preset, en, reset
endmodule

module AbstractedFlipFlops (
  input  S,
  input  D,
  input  R,
  output Q,
  output Q_2,
  output nQ,
  output nQ_2
);

  wire clock_1_out, clock_2_out;

  Clock clock_1 (.out(clock_1_out));
  S_R_Flip_Flop s_r_ff_1 (.S(S), .clk(clock_1_out), .R(R), .Q(Q_2), .Qn(nQ_2));  // open: preset, reset, en
  Clock clock_2 (.out(clock_2_out));
  D_Flip_Flop d_ff_1 (.clk(clock_2_out), .D(D), .Q(Q), .Qn(nQ));  // open: preset, en, reset
endmodule

module _2bitRegister (
  input  Load,
  input  [1:0] Data_In,
  output [1:0] Register_s_Data
);

  wire and_1_out, clock_1_out;

  Clock clock_1 (.out(clock_1_out));
  and and_1 (and_1_out, clock_1_out, Load);
  D_Flip_Flop d_ff_1 (.clk(and_1_out), .D(Data_In[0]), .Q(Register_s_Data[0]));  // open: Qn, preset, en, reset
  D_Flip_Flop d_ff_2 (.clk(and_1_out), .D(Data_In[1]), .Q(Register_s_Data[1]));  // open: Qn, preset, en, reset
endmodule

module _4bitRegister (
  input  Load,
  input  [3:0] Data_In,
  output [3:0] Register_s_Data
);

  wire and_1_out, clock_1_out;

  Clock clock_1 (.out(clock_1_out));
  and and_1 (and_1_out, clock_1_out, Load);
  D_Flip_Flop d_ff_1 (.clk(and_1_out), .D(Data_In[0]), .Q(Register_s_Data[0]));  // open: Qn, preset, en, reset
  D_Flip_Flop d_ff_2 (.clk(and_1_out), .D(Data_In[1]), .Q(Register_s_Data[1]));  // open: Qn, preset, en, reset
  D_Flip_Flop d_ff_3 (.clk(and_1_out), .D(Data_In[2]), .Q(Register_s_Data[2]));  // open: Qn, preset, en, reset
  D_Flip_Flop d_ff_4 (.clk(and_1_out), .D(Data_In[3]), .Q(Register_s_Data[3]));  // open: Qn, preset, en, reset
endmodule

module _8bitRegister (
  input  Load,
  input  [7:0] Data_In,
  output [7:0] Register_s_Data
);

  wire and_1_out, clock_1_out;

  Clock clock_1 (.out(clock_1_out));
  and and_1 (and_1_out, clock_1_out, Load);
  D_Flip_Flop d_ff_1 (.clk(and_1_out), .D(Data_In[0]), .Q(Register_s_Data[0]));  // open: Qn, preset, en, reset
  D_Flip_Flop d_ff_2 (.clk(and_1_out), .D(Data_In[1]), .Q(Register_s_Data[1]));  // open: Qn, preset, en, reset
  D_Flip_Flop d_ff_3 (.clk(and_1_out), .D(Data_In[2]), .Q(Register_s_Data[2]));  // open: Qn, preset, en, reset
  D_Flip_Flop d_ff_4 (.clk(and_1_out), .D(Data_In[3]), .Q(Register_s_Data[3]));  // open: Qn, preset, en, reset
  D_Flip_Flop d_ff_5 (.clk(and_1_out), .D(Data_In[4]), .Q(Register_s_Data[4]));  // open: Qn, preset, en, reset
  D_Flip_Flop d_ff_6 (.clk(and_1_out), .D(Data_In[5]), .Q(Register_s_Data[5]));  // open: Qn, preset, en, reset
  D_Flip_Flop d_ff_7 (.clk(and_1_out), .D(Data_In[6]), .Q(Register_s_Data[6]));  // open: Qn, preset, en, reset
  D_Flip_Flop d_ff_8 (.clk(and_1_out), .D(Data_In[7]), .Q(Register_s_Data[7]));  // open: Qn, preset, en, reset
endmodule

module AbstractedRegisters (
  input  [1:0] Data_In,
  input  Load,
  input  [3:0] Data_In_2,
  input  [7:0] Data_In_3,
  output [1:0] Register_s_Data,
  output [3:0] Register_s_Data_2,
  output [7:0] Register_s_Data_3
);

  wire and_1_out, clock_1_out;

  Clock clock_1 (.out(clock_1_out));
  and and_1 (and_1_out, Load, clock_1_out);
  Register #(.width(2)) register_1 (.D(Data_In), .Q(Register_s_Data), .clk(and_1_out));  // open: en, clr
  Register #(.width(4)) register_2 (.D(Data_In_2), .Q(Register_s_Data_2), .clk(and_1_out));  // open: en, clr
  Register register_3 (.D(Data_In_3), .Q(Register_s_Data_3), .clk(and_1_out));  // open: en, clr
endmodule

module SRAMCELL (
  input  Data_Line__in,
  input  Word_Enable__in,
  output Value_Stored,
  output Word_Enable__out
);

  wire and_1_out, and_2_out, not_1_out, not_2_out, not_3_out, or_2_out;

  and and_1 (and_1_out, Data_Line__in, Word_Enable__in);
  not not_1 (not_1_out, or_2_out);
  or or_1 (Value_Stored, not_1_out, and_1_out);
  or or_2 (or_2_out, not_2_out, and_2_out);
  not not_2 (not_2_out, Value_Stored);
  not not_3 (not_3_out, Data_Line__in);
  and and_2 (and_2_out, not_3_out, Word_Enable__in);

  assign Word_Enable__out = Word_Enable__in;

  // Notes on the sheet:
  //   Loop
endmodule

module SRAM (
  input  [3:0] Data_Lines,
  input  Word_Enable,
  input  [1:0] Address,
  output [3:0] out_4,
  output [3:0] out_5,
  output [3:0] out_6,
  output [3:0] out_7
);

  wire decoder_1_out0, decoder_1_out1, decoder_1_out2, decoder_1_out3, sramcell_1_word_enable__out,
       sramcell_2_word_enable__out, sramcell_3_word_enable__out, sramcell_4_word_enable__out,
       sramcell_5_word_enable__out, sramcell_6_word_enable__out, sramcell_7_word_enable__out,
       sramcell_8_word_enable__out, sramcell_9_word_enable__out, sramcell_10_word_enable__out,
       sramcell_11_word_enable__out, sramcell_12_word_enable__out;

  Decoder #(.select(2), .disabled(0)) decoder_1 (
    .out0(decoder_1_out0), .out1(decoder_1_out1), .out2(decoder_1_out2), .out3(decoder_1_out3),
    .sel(Address), .en(Word_Enable));
  SRAMCELL sramcell_1 (
    .Data_Line__in(Data_Lines[0]), .Word_Enable__in(decoder_1_out0), .Value_Stored(out_4[0]),
    .Word_Enable__out(sramcell_1_word_enable__out));
  SRAMCELL sramcell_2 (
    .Data_Line__in(Data_Lines[0]), .Word_Enable__in(decoder_1_out1), .Value_Stored(out_5[0]),
    .Word_Enable__out(sramcell_2_word_enable__out));
  SRAMCELL sramcell_3 (
    .Data_Line__in(Data_Lines[0]), .Word_Enable__in(decoder_1_out2), .Value_Stored(out_6[0]),
    .Word_Enable__out(sramcell_3_word_enable__out));
  SRAMCELL sramcell_4 (
    .Data_Line__in(Data_Lines[0]), .Word_Enable__in(decoder_1_out3), .Value_Stored(out_7[0]),
    .Word_Enable__out(sramcell_4_word_enable__out));
  SRAMCELL sramcell_5 (
    .Data_Line__in(Data_Lines[2]), .Word_Enable__in(sramcell_6_word_enable__out), .Value_Stored(out_4[2]),
    .Word_Enable__out(sramcell_5_word_enable__out));
  SRAMCELL sramcell_6 (
    .Data_Line__in(Data_Lines[1]), .Word_Enable__in(sramcell_1_word_enable__out), .Value_Stored(out_4[1]),
    .Word_Enable__out(sramcell_6_word_enable__out));
  SRAMCELL sramcell_7 (
    .Data_Line__in(Data_Lines[2]), .Word_Enable__in(sramcell_8_word_enable__out), .Value_Stored(out_5[2]),
    .Word_Enable__out(sramcell_7_word_enable__out));
  SRAMCELL sramcell_8 (
    .Data_Line__in(Data_Lines[1]), .Word_Enable__in(sramcell_2_word_enable__out), .Value_Stored(out_5[1]),
    .Word_Enable__out(sramcell_8_word_enable__out));
  SRAMCELL sramcell_9 (
    .Data_Line__in(Data_Lines[2]), .Word_Enable__in(sramcell_10_word_enable__out), .Value_Stored(out_6[2]),
    .Word_Enable__out(sramcell_9_word_enable__out));
  SRAMCELL sramcell_10 (
    .Data_Line__in(Data_Lines[1]), .Word_Enable__in(sramcell_3_word_enable__out), .Value_Stored(out_6[1]),
    .Word_Enable__out(sramcell_10_word_enable__out));
  SRAMCELL sramcell_11 (
    .Data_Line__in(Data_Lines[2]), .Word_Enable__in(sramcell_12_word_enable__out), .Value_Stored(out_7[2]),
    .Word_Enable__out(sramcell_11_word_enable__out));
  SRAMCELL sramcell_12 (
    .Data_Line__in(Data_Lines[1]), .Word_Enable__in(sramcell_4_word_enable__out), .Value_Stored(out_7[1]),
    .Word_Enable__out(sramcell_12_word_enable__out));
  SRAMCELL sramcell_13 (
    .Data_Line__in(Data_Lines[3]), .Word_Enable__in(sramcell_5_word_enable__out), .Value_Stored(out_4[3]));  // open: Word_Enable__out
  SRAMCELL sramcell_14 (
    .Data_Line__in(Data_Lines[3]), .Word_Enable__in(sramcell_7_word_enable__out), .Value_Stored(out_5[3]));  // open: Word_Enable__out
  SRAMCELL sramcell_15 (
    .Data_Line__in(Data_Lines[3]), .Word_Enable__in(sramcell_9_word_enable__out), .Value_Stored(out_6[3]));  // open: Word_Enable__out
  SRAMCELL sramcell_16 (
    .Data_Line__in(Data_Lines[3]), .Word_Enable__in(sramcell_11_word_enable__out), .Value_Stored(out_7[3]));  // open: Word_Enable__out

  // Notes on the sheet:
  //   4x4 SRAM
  //   Word at Address 0
  //   Word at Address 1
  //   Word at Address 2
  //   Word at Address 3
endmodule

module RAMExample (
  input  [7:0] Address,
  input  [7:0] Data_to_Store,
  input  Store,
  input  Enable,
  input  Load,
  input  Clear,
  output [7:0] out_7
);

  wire clock_1_out;
  wire [7:0] ram_1_data;

  Clock clock_1 (.out(clock_1_out));
  RAM #(.bus("separate")) ram_1 (
    .addr(Address), .din(Data_to_Store), .data(ram_1_data), .str(Store), .sel(Enable), .clk(clock_1_out),
    .ld(Load), .clr(Clear));
  Register Loaded_Data (.D(ram_1_data), .Q(out_7), .clk(clock_1_out));  // open: en, clr
endmodule
