// Logisim project Module12.circ as structural Verilog: 5 circuits, main circuit main
module main (
  input  Data_Line,
  input  Word_Enable,
  input  [7:0] in_3,
  input  in_4,
  input  [4:0] in_5,
  output [7:0] out_6
);

  wire and_1_out, and_2_out, clock_1_out, not_1_out, not_2_out, not_3_out, not_4_out, or_1_out, or_2_out;

  assign out_6 = in_4 ? in_3 : 8'bz;  // Controlled_Buffer controlled_buffer_1
  Clock clock_1 (.out(clock_1_out));
  not not_1 (not_1_out, or_2_out);
  or or_1 (or_1_out, not_1_out, and_1_out);
  and and_1 (and_1_out, Data_Line, Word_Enable);
  not not_2 (not_2_out, in_4);
  not not_3 (not_3_out, or_1_out);
  or or_2 (or_2_out, not_3_out, and_2_out);
  RAM #(.addrWidth(5)) ram_1 (.addr(in_5), .data(out_6), .clk(clock_1_out), .ld(not_2_out));  // open: sel, clr
  not not_4 (not_4_out, Data_Line);
  and and_2 (and_2_out, not_4_out, Word_Enable);

  // Notes on the sheet:
  //   Loop
endmodule

module SRAM_Cell (
  input  Data_Line,
  input  Word_Enable
);

  wire not_2_out, not_3_out, transistor_1_out;

  Transistor #(.\type ("n"), .gate("br")) transistor_1 (.in(Data_Line), .out(transistor_1_out), .gate(Word_Enable));
  not not_1 (transistor_1_out, not_2_out);
  not not_2 (not_2_out, transistor_1_out);
  not not_3 (not_3_out, Data_Line);
  Transistor #(.\type ("n"), .gate("br")) transistor_2 (.in(not_3_out), .out(not_2_out), .gate(Word_Enable));

  // Notes on the sheet:
  //   Loop
endmodule

module SRAMCELL (
  input  Data_Line__in,
  input  Word_Enable__in,
  output Value_Stored,
  output Word_Enable__out
);

  wire and_1_out, and_2_out, not_1_out, not_2_out, not_3_out, or_2_out;

  and and_1 (and_1_out, Data_Line__in, Word_Enable__in);
  not not_1 (not_1_out, or_2_out);
  or or_1 (Value_Stored, not_1_out, and_1_out);
  not not_2 (not_2_out, Value_Stored);
  or or_2 (or_2_out, not_2_out, and_2_out);
  not not_3 (not_3_out, Data_Line__in);
  and and_2 (and_2_out, not_3_out, Word_Enable__in);

  assign Word_Enable__out = Word_Enable__in;

  // Notes on the sheet:
  //   Loop
endmodule

module SRAM (
  input  [3:0] Data_Lines,
  input  Word_Enable,
  input  [1:0] Address,
  output [3:0] out_4,
  output [3:0] out_5,
  output [3:0] out_6,
  output [3:0] out_7
);

  wire decoder_1_out0, decoder_1_out1, decoder_1_out2, decoder_1_out3, sramcell_1_word_enable__out,
       sramcell_2_word_enable__out, sramcell_3_word_enable__out, sramcell_4_word_enable__out,
       sramcell_5_word_enable__out, sramcell_6_word_enable__out, sramcell_7_word_enable__out,
       sramcell_8_word_enable__out, sramcell_9_word_enable__out, sramcell_10_word_enable__out,
       sramcell_11_word_enable__out, sramcell_12_word_enable__out;

  Decoder #(.select(2), .disabled(0)) decoder_1 (
    .out0(decoder_1_out0), .out1(decoder_1_out1), .out2(decoder_1_out2), .out3(decoder_1_out3),
    .sel(Address), .en(Word_Enable));
  SRAMCELL sramcell_1 (
    .Data_Line__in(Data_Lines[0]), .Word_Enable__in(decoder_1_out0), .Value_Stored(out_4[0]),
    .Word_Enable__out(sramcell_1_word_enable__out));
  SRAMCELL sramcell_2 (
    .Data_Line__in(Data_Lines[0]), .Word_Enable__in(decoder_1_out1), .Value_Stored(out_5[0]),
    .Word_Enable__out(sramcell_2_word_enable__out));
  SRAMCELL sramcell_3 (
    .Data_Line__in(Data_Lines[0]), .Word_Enable__in(decoder_1_out2), .Value_Stored(out_6[0]),
    .Word_Enable__out(sramcell_3_word_enable__out));
  SRAMCELL sramcell_4 (
    .Data_Line__in(Data_Lines[0]), .Word_Enable__in(decoder_1_out3), .Value_Stored(out_7[0]),
    .Word_Enable__out(sramcell_4_word_enable__out));
  SRAMCELL sramcell_5 (
    .Data_Line__in(Data_Lines[2]), .Word_Enable__in(sramcell_6_word_enable__out), .Value_Stored(out_4[2]),
    .Word_Enable__out(sramcell_5_word_enable__out));
  SRAMCELL sramcell_6 (
    .Data_Line__in(Data_Lines[1]), .Word_Enable__in(sramcell_1_word_enable__out), .Value_Stored(out_4[1]),
    .Word_Enable__out(sramcell_6_word_enable__out));
  SRAMCELL sramcell_7 (
    .Data_Line__in(Data_Lines[1]), .Word_Enable__in(sramcell_2_word_enable__out), .Value_Stored(out_5[1]),
    .Word_Enable__out(sramcell_7_word_enable__out));
  SRAMCELL sramcell_8 (
    .Data_Line__in(Data_Lines[2]), .Word_Enable__in(sramcell_7_word_enable__out), .Value_Stored(out_5[2]),
    .Word_Enable__out(sramcell_8_word_enable__out));
  SRAMCELL sramcell_9 (
    .Data_Line__in(Data_Lines[1]), .Word_Enable__in(sramcell_3_word_enable__out), .Value_Stored(out_6[1]),
    .Word_Enable__out(sramcell_9_word_enable__out));
  SRAMCELL sramcell_10 (
    .Data_Line__in(Data_Lines[2]), .Word_Enable__in(sramcell_9_word_enable__out), .Value_Stored(out_6[2]),
    .Word_Enable__out(sramcell_10_word_enable__out));
  SRAMCELL sramcell_11 (
    .Data_Line__in(Data_Lines[1]), .Word_Enable__in(sramcell_4_word_enable__out), .Value_Stored(out_7[1]),
    .Word_Enable__out(sramcell_11_word_enable__out));
  SRAMCELL sramcell_12 (
    .Data_Line__in(Data_Lines[2]), .Word_Enable__in(sramcell_11_word_enable__out), .Value_Stored(out_7[2]),
    .Word_Enable__out(sramcell_12_word_enable__out));
  SRAMCELL sramcell_13 (
    .Data_Line__in(Data_Lines[3]), .Word_Enable__in(sramcell_5_word_enable__out), .Value_Stored(out_4[3]));  // open: Word_Enable__out
  SRAMCELL sramcell_14 (
    .Data_Line__in(Data_Lines[3]), .Word_Enable__in(sramcell_8_word_enable__out), .Value_Stored(out_5[3]));  // open: Word_Enable__out
  SRAMCELL sramcell_15 (
    .Data_Line__in(Data_Lines[3]), .Word_Enable__in(sramcell_10_word_enable__out), .Value_Stored(out_6[3]));  // open: Word_Enable__out
  SRAMCELL sramcell_16 (
    .Data_Line__in(Data_Lines[3]), .Word_Enable__in(sramcell_12_word_enable__out), .Value_Stored(out_7[3]));  // open: Word_Enable__out

  // Notes on the sheet:
  //   4x4 SRAM
  //   Word at Address 0
  //   Word at Address 1
  //   Word at Address 2
  //   Word at Address 3
endmodule

module DRAM_Cell (
  input  Data_Line,
  input  Word_Enable
);

  wire not_1_out;

  Transistor #(.\type ("n"), .gate("br")) transistor_1 (.in(Data_Line), .gate(Word_Enable));  // open: out
  not not_1 (not_1_out, Data_Line);
  Transistor #(.\type ("n"), .gate("br")) transistor_2 (.in(not_1_out), .gate(Word_Enable));  // open: out
endmodule
