// Logisim project Module6.circ as structural Verilog: 9 circuits, main circuit Gates
module Bus1 (
  input  [15:0] _16_bit_Bus,
  output [3:0] _4_bit_Bus,
  output [3:0] _4_bit_Bus_2,
  output [3:0] _4_bit_Bus_3,
  output [3:0] _4_bit_Bus_4
);


  assign _4_bit_Bus = _16_bit_Bus[3:0];
  assign _4_bit_Bus_2 = _16_bit_Bus[7:4];
  assign _4_bit_Bus_3 = _16_bit_Bus[11:8];
  assign _4_bit_Bus_4 = _16_bit_Bus[15:12];

  // Notes on the sheet:
  //   Split to two 8-bit busses
  //   Split to two 4-bit busses
  //   Split to two 4-bit busses
endmodule

module Bus2 (
  input  [3:0] _4_bit_Bus,
  input  [3:0] _4_bit_Bus_2,
  input  [3:0] _4_bit_Bus_3,
  input  [3:0] _4_bit_Bus_4,
  output [15:0] out_5
);


  assign out_5 = {_4_bit_Bus_4, _4_bit_Bus_3, _4_bit_Bus_2, _4_bit_Bus};

  // Notes on the sheet:
  //   Bundle to one 8-bit bus
  //   Bundle to one 8-bit bus
  //   Bundle to one 16-bit bus
endmodule

module Bus3 (
  input  [3:0] _4_bit_Bus,
  input  [3:0] _4_bit_Bus_2,
  input  [3:0] _4_bit_Bus_3,
  input  [3:0] _4_bit_Bus_4,
  output [15:0] out_5
);


  assign out_5 = {_4_bit_Bus_4, _4_bit_Bus_3, _4_bit_Bus_2, _4_bit_Bus};

  // Notes on the sheet:
  //   Bundle to one 16-bit bus
endmodule

module Gates (
  input  x,
  input  x_2,
  input  y,
  input  y_2,
  input  x_3,
  input  x_4,
  input  y_3,
  input  y_4,
  input  x_5,
  input  NOT,
  input  y_5,
  input  x_6,
  input  y_6,
  output out_14,
  output out_15,
  output out_16,
  output out_17,
  output out_18,
  output out_19,
  output out_20
);

  and and_1 (out_14, x, y);
  or or_1 (out_16, x_3, y_3);
  not not_1 (out_18, NOT);
  nand nand_1 (out_20, x_6, y_6);
  xor xor_1 (out_15, x_2, y_2);
  nor nor_1 (out_19, x_5, y_5);
  xnor xnor_1 (out_17, x_4, y_4);

  // Notes on the sheet:
  //   AND
  //   OR
  //   NAND
  //   XOR
  //   XNOR
  //   NOR
endmodule

module Sample (
  input  x,
  input  y,
  input  z,
  output F
);

  wire not_1_out, or_1_out, xor_1_out;

  not not_1 (not_1_out, z);
  or or_1 (or_1_out, y, x);
  xor xor_1 (xor_1_out, z, y);
  and and_1 (F, not_1_out, xor_1_out, or_1_out);

  // Notes on the sheet:
  //   (x+y)(y xor z)(~z)
endmodule

module Practice1 (
);


  // Notes on the sheet:
  //   Create a logic circuit for: x + ~(xy)
endmodule

module Practice2 (
);


  // Notes on the sheet:
  //   Create a logic circuit for: (x+y)(x+z)
endmodule

module Practice3 (
);


  // Notes on the sheet:
  //   Create a logic circuit for: (~x)(~y)z + ~(xy+xz)
endmodule

module Practice4 (
);


  // Notes on the sheet:
  //   Create a logic circuit for: (x + y)(~x + y + ~z)
endmodule
