// Logisim project Module8.circ as structural Verilog: 11 circuits, main circuit 2bitMultiplier
module _2bitMultiplier (
  input  X_1,
  input  X_0,
  input  Y_0,
  input  Y_1,
  output P_0,
  output P_1,
  output P_2,
  output P_3
);

  wire adder_1_cout, and_1_out, and_2_out, and_3_out;

  and and_1 (and_1_out, Y_1, X_1);
  and and_2 (and_2_out, Y_1, X_0);
  and and_3 (and_3_out, Y_0, X_1);
  and and_4 (P_0, Y_0, X_0);
  Adder #(.width(1)) adder_1 (.a(and_3_out), .b(and_2_out), .out(P_1), .cout(adder_1_cout));  // open: cin
  Adder #(.width(1)) adder_2 (.a(adder_1_cout), .b(and_1_out), .out(P_2), .cout(P_3));  // open: cin
endmodule

module _3bitMultiplier (
  input  X_2,
  input  X_1,
  input  X_0,
  input  Y_0,
  input  Y_1,
  input  Y_2,
  output P_0,
  output P_1,
  output P_2,
  output P_3,
  output P_4,
  output P_5
);

  wire adder_1_cout, adder_2_cout, adder_2_out, adder_3_cout, adder_3_out, adder_4_cout, adder_5_cout,
       and_1_out, and_2_out, and_3_out, and_4_out, and_5_out, and_6_out, and_7_out, and_9_out;

  and and_1 (and_1_out, Y_2, X_2);
  and and_2 (and_2_out, Y_2, X_0);
  and and_3 (and_3_out, Y_2, X_1);
  and and_4 (and_4_out, Y_1, X_2);
  and and_5 (and_5_out, Y_1, X_1);
  and and_6 (and_6_out, Y_0, X_2);
  and and_7 (and_7_out, Y_1, X_0);
  and and_8 (P_0, Y_0, X_0);
  and and_9 (and_9_out, Y_0, X_1);
  Adder #(.width(1)) adder_1 (.a(and_9_out), .b(and_7_out), .out(P_1), .cout(adder_1_cout));  // open: cin
  Adder #(.width(1)) adder_2 (.a(and_6_out), .b(and_5_out), .out(adder_2_out), .cout(adder_2_cout));  // open: cin
  Adder #(.width(1)) adder_3 (.a(and_4_out), .b(and_3_out), .out(adder_3_out), .cin(adder_2_cout), .cout(adder_3_cout));
  Adder #(.width(1)) adder_4 (.a(adder_2_out), .b(and_2_out), .out(P_2), .cin(adder_1_cout), .cout(adder_4_cout));
  Adder #(.width(1)) adder_5 (.a(adder_4_cout), .b(adder_3_out), .out(P_3), .cout(adder_5_cout));  // open: cin
  Adder #(.width(1)) adder_6 (.a(adder_3_cout), .b(and_1_out), .out(P_4), .cin(adder_5_cout), .cout(P_5));
endmodule

module SRLatch (
  input  S,
  input  R,
  output nQ,
  output Q
);

  nor nor_1 (nQ, S, Q);
  nor nor_2 (Q, nQ, R);
endmodule

module SRFlipFlop (
  input  S,
  input  R,
  output nQ,
  output Q
);

  wire and_1_out, and_2_out, clock_1_out;

  Clock clock_1 (.out(clock_1_out));
  and and_1 (and_1_out, S, clock_1_out);
  and and_2 (and_2_out, clock_1_out, R);
  nor nor_1 (nQ, and_1_out, Q);
  nor nor_2 (Q, nQ, and_2_out);
endmodule

module DFlipFlop (
  input  D,
  output nQ,
  output Q
);

  wire and_1_out, and_2_out, clock_1_out, not_1_out;

  Clock clock_1 (.out(clock_1_out));
  not not_1 (not_1_out, D);
  and and_1 (and_1_out, D, clock_1_out);
  and and_2 (and_2_out, clock_1_out, not_1_out);
  nor nor_1 (nQ, and_1_out, Q);
  nor nor_2 (Q, nQ, and_2_out);
endmodule

module JKFlipFlop (
  input  J,
  input  K,
  output Q,
  output nQ
);

  wire clock_1_out;

  Clock clock_1 (.out(clock_1_out));
  J_K_Flip_Flop j_k_ff_1 (.J(J), .clk(clock_1_out), .K(K), .Q(Q), .Qn(nQ));  // open: preset, en, reset
endmodule

module AbstractedFlipFlops (
  input  S,
  input  D,
  input  R,
  output Q,
  output Q_2,
  output nQ,
  output nQ_2
);

  wire clock_1_out, clock_2_out;

  Clock clock_1 (.out(clock_1_out));
  S_R_Flip_Flop s_r_ff_1 (.S(S), .clk(clock_1_out), .R(R), .Q(Q_2), .Qn(nQ_2));  // open: preset, reset, en
  Clock clock_2 (.out(clock_2_out));
  D_Flip_Flop d_ff_1 (.clk(clock_2_out), .D(D), .Q(Q), .Qn(nQ));  // open: preset, en, reset
endmodule

module _2bitRegister (
  input  Load,
  input  [1:0] Data_In,
  output [1:0] Register_s_Data
);

  wire and_1_out, clock_1_out;

  Clock clock_1 (.out(clock_1_out));
  and and_1 (and_1_out, clock_1_out, Load);
  D_Flip_Flop d_ff_1 (.clk(and_1_out), .D(Data_In[0]), .Q(Register_s_Data[0]));  // open: Qn, preset, en, reset
  D_Flip_Flop d_ff_2 (.clk(and_1_out), .D(Data_In[1]), .Q(Register_s_Data[1]));  // open: Qn, preset, en, reset
endmodule

module _4bitRegister (
  input  Load,
  input  [3:0] Data_In,
  output [3:0] Register_s_Data
);

  wire and_1_out, clock_1_out;

  Clock clock_1 (.out(clock_1_out));
  and and_1 (and_1_out, clock_1_out, Load);
  D_Flip_Flop d_ff_1 (.clk(and_1_out), .D(Data_In[0]), .Q(Register_s_Data[0]));  // open: Qn, preset, en, reset
  D_Flip_Flop d_ff_2 (.clk(and_1_out), .D(Data_In[1]), .Q(Register_s_Data[1]));  // open: Qn, preset, en, reset
  D_Flip_Flop d_ff_3 (.clk(and_1_out), .D(Data_In[2]), .Q(Register_s_Data[2]));  // open: Qn, preset, en, reset
  D_Flip_Flop d_ff_4 (.clk(and_1_out), .D(Data_In[3]), .Q(Register_s_Data[3]));  // open: Qn, preset, en, reset
endmodule

module _8bitRegister (
  input  Load,
  input  [7:0] Data_In,
  output [7:0] Register_s_Data
);

  wire and_1_out, clock_1_out;

  Clock clock_1 (.out(clock_1_out));
  and and_1 (and_1_out, clock_1_out, Load);
  D_Flip_Flop d_ff_1 (.clk(and_1_out), .D(Data_In[0]), .Q(Register_s_Data[0]));  // open: Qn, preset, en, reset
  D_Flip_Flop d_ff_2 (.clk(and_1_out), .D(Data_In[1]), .Q(Register_s_Data[1]));  // open: Qn, preset, en, reset
  D_Flip_Flop d_ff_3 (.clk(and_1_out), .D(Data_In[2]), .Q(Register_s_Data[2]));  // open: Qn, preset, en, reset
  D_Flip_Flop d_ff_4 (.clk(and_1_out), .D(Data_In[3]), .Q(Register_s_Data[3]));  // open: Qn, preset, en, reset
  D_Flip_Flop d_ff_5 (.clk(and_1_out), .D(Data_In[4]), .Q(Register_s_Data[4]));  // open: Qn, preset, en, reset
  D_Flip_Flop d_ff_6 (.clk(and_1_out), .D(Data_In[5]), .Q(Register_s_Data[5]));  // open: Qn, preset, en, reset
  D_Flip_Flop d_ff_7 (.clk(and_1_out), .D(Data_In[6]), .Q(Register_s_Data[6]));  // open: Qn, preset, en, reset
  D_Flip_Flop d_ff_8 (.clk(and_1_out), .D(Data_In[7]), .Q(Register_s_Data[7]));  // open: Qn, preset, en, reset
endmodule

module AbstractedRegisters (
  input  [1:0] Data_In,
  input  Load,
  input  [3:0] Data_In_2,
  input  [7:0] Data_In_3,
  output [1:0] Register_s_Data,
  output [3:0] Register_s_Data_2,
  output [7:0] Register_s_Data_3
);

  wire and_1_out, clock_1_out;

  Clock clock_1 (.out(clock_1_out));
  and and_1 (and_1_out, Load, clock_1_out);
  Register #(.width(2)) register_1 (.D(Data_In), .Q(Register_s_Data), .clk(and_1_out));  // open: en, clr
  Register #(.width(4)) register_2 (.D(Data_In_2), .Q(Register_s_Data_2), .clk(and_1_out));  // open: en, clr
  Register register_3 (.D(Data_In_3), .Q(Register_s_Data_3), .clk(and_1_out));  // open: en, clr
endmodule
