// Logisim project Module9.circ as structural Verilog: 3 circuits, main circuit SRAMCELL
module SRAMCELL (
  input  Data_Line__in,
  input  Word_Enable__in,
  output Value_Stored,
  output Word_Enable__out
);

  wire and_1_out, and_2_out, not_1_out, not_2_out, not_3_out, or_2_out;

  and and_1 (and_1_out, Data_Line__in, Word_Enable__in);
  not not_1 (not_1_out, or_2_out);
  or or_1 (Value_Stored, not_1_out, and_1_out);
  or or_2 (or_2_out, not_2_out, and_2_out);
  not not_2 (not_2_out, Value_Stored);
  not not_3 (not_3_out, Data_Line__in);
  and and_2 (and_2_out, not_3_out, Word_Enable__in);

  assign Word_Enable__out = Word_Enable__in;

  // Notes on the sheet:
  //   Loop
endmodule

module SRAM (
  input  [3:0] Data_Lines,
  input  Word_Enable,
  input  [1:0] Address,
  output [3:0] out_4,
  output [3:0] out_5,
  output [3:0] out_6,
  output [3:0] out_7
);

  wire decoder_1_out0, decoder_1_out1, decoder_1_out2, decoder_1_out3, sramcell_1_word_enable__out,
       sramcell_2_word_enable__out, sramcell_3_word_enable__out, sramcell_4_word_enable__out,
       sramcell_5_word_enable__out, sramcell_6_word_enable__out, sramcell_7_word_enable__out,
       sramcell_8_word_enable__out, sramcell_9_word_enable__out, sramcell_10_word_enable__out,
       sramcell_11_word_enable__out, sramcell_12_word_enable__out;

  Decoder #(.select(2), .disabled(0)) decoder_1 (
    .out0(decoder_1_out0), .out1(decoder_1_out1), .out2(decoder_1_out2), .out3(decoder_1_out3),
    .sel(Address), .en(Word_Enable));
  SRAMCELL sramcell_1 (
    .Data_Line__in(Data_Lines[0]), .Word_Enable__in(decoder_1_out0), .Value_Stored(out_4[0]),
    .Word_Enable__out(sramcell_1_word_enable__out));
  SRAMCELL sramcell_2 (
    .Data_Line__in(Data_Lines[0]), .Word_Enable__in(decoder_1_out1), .Value_Stored(out_5[0]),
    .Word_Enable__out(sramcell_2_word_enable__out));
  SRAMCELL sramcell_3 (
    .Data_Line__in(Data_Lines[0]), .Word_Enable__in(decoder_1_out2), .Value_Stored(out_6[0]),
    .Word_Enable__out(sramcell_3_word_enable__out));
  SRAMCELL sramcell_4 (
    .Data_Line__in(Data_Lines[0]), .Word_Enable__in(decoder_1_out3), .Value_Stored(out_7[0]),
    .Word_Enable__out(sramcell_4_word_enable__out));
  SRAMCELL sramcell_5 (
    .Data_Line__in(Data_Lines[1]), .Word_Enable__in(sramcell_1_word_enable__out), .Value_Stored(out_4[1]),
    .Word_Enable__out(sramcell_5_word_enable__out));
  SRAMCELL sramcell_6 (
    .Data_Line__in(Data_Lines[2]), .Word_Enable__in(sramcell_5_word_enable__out), .Value_Stored(out_4[2]),
    .Word_Enable__out(sramcell_6_word_enable__out));
  SRAMCELL sramcell_7 (
    .Data_Line__in(Data_Lines[2]), .Word_Enable__in(sramcell_8_word_enable__out), .Value_Stored(out_5[2]),
    .Word_Enable__out(sramcell_7_word_enable__out));
  SRAMCELL sramcell_8 (
    .Data_Line__in(Data_Lines[1]), .Word_Enable__in(sramcell_2_word_enable__out), .Value_Stored(out_5[1]),
    .Word_Enable__out(sramcell_8_word_enable__out));
  SRAMCELL sramcell_9 (
    .Data_Line__in(Data_Lines[1]), .Word_Enable__in(sramcell_3_word_enable__out), .Value_Stored(out_6[1]),
    .Word_Enable__out(sramcell_9_word_enable__out));
  SRAMCELL sramcell_10 (
    .Data_Line__in(Data_Lines[2]), .Word_Enable__in(sramcell_9_word_enable__out), .Value_Stored(out_6[2]),
    .Word_Enable__out(sramcell_10_word_enable__out));
  SRAMCELL sramcell_11 (
    .Data_Line__in(Data_Lines[2]), .Word_Enable__in(sramcell_12_word_enable__out), .Value_Stored(out_7[2]),
    .Word_Enable__out(sramcell_11_word_enable__out));
  SRAMCELL sramcell_12 (
    .Data_Line__in(Data_Lines[1]), .Word_Enable__in(sramcell_4_word_enable__out), .Value_Stored(out_7[1]),
    .Word_Enable__out(sramcell_12_word_enable__out));
  SRAMCELL sramcell_13 (
    .Data_Line__in(Data_Lines[3]), .Word_Enable__in(sramcell_6_word_enable__out), .Value_Stored(out_4[3]));  // open: Word_Enable__out
  SRAMCELL sramcell_14 (
    .Data_Line__in(Data_Lines[3]), .Word_Enable__in(sramcell_7_word_enable__out), .Value_Stored(out_5[3]));  // open: Word_Enable__out
  SRAMCELL sramcell_15 (
    .Data_Line__in(Data_Lines[3]), .Word_Enable__in(sramcell_10_word_enable__out), .Value_Stored(out_6[3]));  // open: Word_Enable__out
  SRAMCELL sramcell_16 (
    .Data_Line__in(Data_Lines[3]), .Word_Enable__in(sramcell_11_word_enable__out), .Value_Stored(out_7[3]));  // open: Word_Enable__out

  // Notes on the sheet:
  //   4x4 SRAM
  //   Word at Address 0
  //   Word at Address 1
  //   Word at Address 2
  //   Word at Address 3
endmodule

module RAMExample (
  input  [7:0] Address,
  input  [7:0] Data_to_Store,
  input  Store,
  input  Enable,
  input  Load,
  input  Clear,
  output [7:0] out_7
);

  wire clock_1_out;
  wire [7:0] ram_1_data;

  Clock clock_1 (.out(clock_1_out));
  RAM #(.bus("separate")) ram_1 (
    .addr(Address), .din(Data_to_Store), .data(ram_1_data), .str(Store), .sel(Enable), .clk(clock_1_out),
    .ld(Load), .clr(Clear));
  Register Loaded_Data (.D(ram_1_data), .Q(out_7), .clk(clock_1_out));  // open: en, clr
endmodule
